// Digital circuit gated_latch.dig as structural Verilog
module gated_latch (
  input  in_1,
  input  in_2,
  output out_3
);

  wire and_1_out, and_2_out, not_1_out, not_2_out, or_1_out;

  not not_1 (not_1_out, in_1);
  and and_1 (and_1_out, in_1, in_2);
  and and_2 (and_2_out, not_1_out, in_2);
  not not_2 (not_2_out, and_2_out);
  or or_1 (or_1_out, out_3, and_1_out);
  and and_3 (out_3, or_1_out, not_2_out);
endmodule
